// Logisim project Ctl_Load_Store.circ as structural Verilog: 1 circuit, main circuit Load_Store
module Load_Store (
  input  Enable,
  input  [15:0] Instruction,
  input  Clk,
  input  Reset,
  input  [31:0] Stack_Pointer,
  input  [31:0] A_Bus,
  input  [31:0] B_Bus,
  output Store,
  output Load,
  output PC_Hold,
  output [2:0] Rd,
  output [2:0] Rm,
  output [2:0] Rn,
  output [31:0] RAM_Addr
);

  wire and_2_out, and_3_out, and_4_out, d_ff_1_q, Is_Register, not_1_out, or_1_out, or_2_out, or_3_out, PC_H;
  wire [2:0] multiplexer_5_out, multiplexer_7_out, multiplexer_9_out, Rt;
  wire [31:0] adder_1_out, adder_2_out, bit_extender_1_out, multiplexer_2_out, multiplexer_3_out,
       register_1_q, shifter_1_out;

  and and_1 (Is_Register, ~Instruction[15], Instruction[14], ~Instruction[13], Instruction[12]);  // AND_Gate
  Shifter #(.shift("ar"), .width(32)) shifter_1 (.in(A_Bus), .\dist (5'b00010), .out(shifter_1_out));
  Multiplexer #(.width(3)) multiplexer_1 (.in0(Instruction[10:8]), .in1(Instruction[2:0]), .out(Rt), .sel(Is_Register));
  Adder #(.width(32)) adder_1 (.a(shifter_1_out), .b(B_Bus), .out(adder_1_out));  // open: cin, cout
  Register #(.width(32)) register_1 (.D(adder_1_out), .en(PC_H), .clk(Clk), .Q(register_1_q), .clr(not_1_out));
  not not_1 (not_1_out, Is_Register);
  Multiplexer #(.width(32)) multiplexer_2 (.in0(register_1_q), .in1(adder_1_out), .out(multiplexer_2_out), .sel(PC_H));
  and and_2 (and_2_out, or_2_out, ~d_ff_1_q);  // AND_Gate
  D_Flip_Flop #(.trigger("falling")) d_ff_1 (
    .D(and_2_out), .clk(Clk), .Q(d_ff_1_q), .Qn(PC_H), .reset(or_1_out));  // open: preset
  or or_1 (or_1_out, Reset, ~Enable, ~or_2_out);  // OR_Gate
  or or_2 (or_2_out, Is_Register, Instruction[11]);
  and and_3 (and_3_out, ~Instruction[11], Is_Register);  // AND_Gate
  or or_3 (or_3_out, Instruction[11], PC_H);
  and and_4 (and_4_out, or_3_out, Is_Register);
  assign bit_extender_1_out = {{24{Instruction[7]}}, Instruction[7:0]};  // Bit_Extender bit_extender_1
  Adder #(.width(32)) adder_2 (.a(Stack_Pointer), .b(bit_extender_1_out), .out(adder_2_out));  // open: cin, cout
  Multiplexer #(.width(32)) multiplexer_3 (
    .in0(adder_2_out), .in1(multiplexer_2_out), .out(multiplexer_3_out), .sel(Is_Register));
  and and_5 (Store, Enable, ~Instruction[11]);  // AND_Gate
  and and_6 (Load, Enable, Instruction[11], d_ff_1_q);
  and and_7 (PC_Hold, Enable, or_2_out, PC_H);
  Multiplexer #(.width(3)) multiplexer_4 (.in0(3'b000), .in1(multiplexer_5_out), .out(Rd), .sel(Enable));
  Multiplexer #(.width(3)) multiplexer_5 (.in0(Rt), .in1(Instruction[8:6]), .out(multiplexer_5_out), .sel(and_3_out));
  Multiplexer #(.width(3)) multiplexer_6 (.in0(3'b000), .in1(multiplexer_7_out), .out(Rm), .sel(Enable));
  Multiplexer #(.width(3)) multiplexer_7 (.in0(Rt), .in1(Instruction[8:6]), .out(multiplexer_7_out), .sel(and_4_out));
  Multiplexer #(.width(3)) multiplexer_8 (.in0(3'b000), .in1(multiplexer_9_out), .out(Rn), .sel(Enable));
  Multiplexer #(.width(3)) multiplexer_9 (.in0(Rt), .in1(Instruction[5:3]), .out(multiplexer_9_out), .sel(and_4_out));
  Multiplexer #(.width(32)) multiplexer_10 (.in0({32{1'b0}}), .in1(multiplexer_3_out), .out(RAM_Addr), .sel(Enable));

  // Other names for the same wires on the sheet: Clock = Clk; Imm8[7:0] = Instruction[7:0];
  //   Rn_t[2:0] = Instruction[5:3]; Rm_t[2:0] = Instruction[8:6]; Load_t = Instruction[11]; Sp[31:0] = Stack_Pointer

  // Notes on the sheet:
  //   Instruction: pull=down
  //   Delay load and hold PC for 1 cycle for the RAM to send out requested data 
endmodule
